# Fritzing sketch esp32_button_panel_module (saved by Fritzing 1.0.3b)
perfboards: 1

parts:
  R1 = Resistor [tolerance=±5% power=0.25W resistance=1k package=THT]
  R2 = Resistor [tolerance=±5% power=0.25W resistance=1k package=THT]  # not connected
  LED1 = LED - 3mm [color="Green (555nm)" current=30mA package="3 mm [THT]"]  # not connected
  LED2 = LED - 3mm [color="Green (555nm)" current=30mA package="3 mm [THT]"]  # not connected
  LED3 = LED - 3mm [color="Green (555nm)" current=30mA package="3 mm [THT]"]  # not connected
  LED4 = LED - 3mm [color="Green (555nm)" current=30mA package="3 mm [THT]"]  # not connected
  LED5 = LED - 3mm [color="Green (555nm)" current=30mA package="3 mm [THT]"]  # not connected
  LED6 = LED - 3mm [color="Green (555nm)" current=30mA package="3 mm [THT]"]
  LED7 = LED - 3mm [color="Red (633nm)" current=30mA package="3 mm [THT]"]
  LED8 = LED - 3mm [color="Yellow (592nm)" current=30mA package="3 mm [THT]"]  # not connected
  S1 = Pushbutton [package="[THT]"]
  S2 = Pushbutton [package="[THT]"]
  S3 = Pushbutton [package="[THT]"]
  S4 = Pushbutton [package="[THT]"]
  S5 = Pushbutton [package="[THT]"]
  S6 = Pushbutton [package="[THT]"]

nets:
  N1: R1.Pin_1, LED6.anode, LED7.anode
  N2: S1.Pin_1, S1.Pin_2
  N3: S1.Pin_3, S1.Pin_4
  N4: S2.Pin_1, S2.Pin_2
  N5: S2.Pin_3, S2.Pin_4
  N6: S3.Pin_1, S3.Pin_2
  N7: S3.Pin_3, S3.Pin_4
  N8: S4.Pin_1, S4.Pin_2
  N9: S4.Pin_3, S4.Pin_4
  N10: S5.Pin_1, S5.Pin_2
  N11: S5.Pin_3, S5.Pin_4
  N12: S6.Pin_1, S6.Pin_2
  N13: S6.Pin_3, S6.Pin_4
