# Fritzing sketch PowerButton-sketch (saved by Fritzing 1.0.3b)
breadboards: 1

parts:
  Raspberry_Pi_1 = Raspberry Pi 3 [part_number=RPI-3-V1.2]
  LED3 = LED - 5mm [color="Red (633nm)" current=0.030A package="5 mm [THT]"]
  LED4 = LED - 5mm [color="Green (555nm)" current=0.030A package="5 mm [THT]"]
  R1 = Resistor [tolerance=±5% power=0.25W resistance=220 package=THT]
  S1 = Momentary Switch [package=ksa_sealed_tac_switch]

nets:
  N1: Raspberry_Pi_1.GPIO3, S1.3, S1.4
  N2: Raspberry_Pi_1.GPIO4, LED3.anode
  N3: Raspberry_Pi_1.GND, S1.1, S1.2
  N4: Raspberry_Pi_1.GPIO14, LED4.anode
  N5: LED3.cathode, LED4.cathode, R1.Pin_1
