# Fritzing sketch esp32_mcp23017_buttons_leds_switches (saved by Fritzing 1.0.3b)
perfboards: 1

parts:
  S1 = Pushbutton [package="[SMD]"]
  S2 = Pushbutton [package="[THT]"]
  S3 = Pushbutton [package="[THT]"]
  S4 = Pushbutton [package="[THT]"]
  S5 = Pushbutton [package="[THT]"]
  S6 = Pushbutton [package="[THT]"]
  S7 = Pushbutton [package="[THT]"]
  LED1 = LED - 3mm [color="Green (565nm)" current=30mA package="3 mm [THT]"]  # not connected
  LED2 = LED - 3mm [color="Red (633nm)" current=0.030A package="3 mm [THT]"]
  LED3 = LED - 3mm [color="Green (565nm)" current=0.030A package="3 mm [THT]"]
  LED4 = LED - 3mm [color="Green (565nm)" current=0.030A package="3 mm [THT]"]
  LED5 = LED - 3mm [color="Green (565nm)" current=0.030A package="3 mm [THT]"]  # not connected
  LED6 = LED - 3mm [color="Green (565nm)" current=0.030A package="3 mm [THT]"]  # not connected
  LED7 = LED - 3mm [color="Green (565nm)" current=0.030A package="3 mm [THT]"]  # not connected
  LED8 = LED - 3mm [color="Green (565nm)" current=0.030A package="3 mm [THT]"]  # not connected
  LED9 = LED - 3mm [color="Yellow (595nm)" current=0.030A package="3 mm [THT]"]  # not connected
  R1 = Resistor [tolerance=±5% power=0.25W resistance=1k package=THT]
  U1 = MCP23017 [package="DIP (Dual Inline) [THT]"]
  R2 = Resistor [tolerance=±5% power=0.25W resistance=1k package=THT]

nets:
  N1: S1.Pin_1, S1.Pin_2, R1.Pin_0
  N2: S1.Pin_3, S1.Pin_4
  N3: S2.Pin_1, S2.Pin_2, U1.GPB0
  N4: S2.Pin_3, S2.Pin_4
  N5: S3.Pin_1, S3.Pin_2, U1.GPB1
  N6: S3.Pin_3, S3.Pin_4
  N7: S4.Pin_1, S4.Pin_2
  N8: S4.Pin_3, S4.Pin_4
  N9: S5.Pin_1, S5.Pin_2
  N10: S5.Pin_3, S5.Pin_4
  N11: S6.Pin_1, S6.Pin_2
  N12: S6.Pin_3, S6.Pin_4
  N13: S7.Pin_1, S7.Pin_2, U1.CS, U1.A0, U1.A1, U1.A2, R2.Pin_0
  N14: S7.Pin_3, S7.Pin_4
  N15: LED2.cathode, R1.Pin_1
  N16: LED3.cathode, R2.Pin_1
  N17: LED3.anode, U1.GPA7
  N18: LED4.anode, U1.GPA6
  N19: U1.GND, U1.RST

notes:
  4 wires from RPi
  4 wires from M5Dial
  3 wires to motion sensor

custom parts:
  MCP23017: 16 bit I/O chip controlled via I2C
